# Fritzing sketch lasertag (saved by Fritzing 0.9.2b)
breadboards: 1

parts:
  Bauteil1 = Arduino Uno (Rev3)
  S1 = Pushbutton [package="[THT]"]
  R1 = Resistor [tolerance=±5% resistance=1k package=THT]
  Q1 = Basic FET P-Channel [package="TO220 [THT]"]
  LED1 = LED - 5mm [color="Red (633nm)" package="5 mm [THT]"]
  R2 = Resistor [tolerance=±5% resistance=1k package=THT]
  IR1 = TSOP312.., 314.. [package=THT]
  IR2 = TSOP312.., 314.. [package=THT]
  IR3 = TSOP312.., 314.. [package=THT]
  R3 = Resistor [tolerance=±5% resistance=3.3k package=THT]

nets:
  GND: Bauteil1.D11_PWM/MOSI, IR1.GND, IR2.GND, IR3.GND, R3.Pin_1
  N1: Bauteil1.D2, S1.Pin_3, S1.Pin_4, R1.Pin_0
  N2: Bauteil1.D3_PWM, Q1.gate
  N3: Bauteil1.5V, S1.Pin_1, S1.Pin_2, Q1.drain, IR1.Data, IR2.Data, IR3.Data, R3.Pin_0
  N4: Bauteil1.GND, R1.Pin_1, R2.Pin_1, IR1.Vs, IR2.Vs, IR3.Vs
  N5: Q1.source, LED1.anode
  N6: LED1.cathode, R2.Pin_0

notes:
  Empfänger
  links: Daten an Pin 11
  mitte: GND
  rechts: 5V
  Trigger an Pin 2
  IR LED an Pin 3
